# Fritzing sketch circuit (saved by Fritzing 0.9.1b)
breadboards: 1

parts:
  Composant1 = Arduino Uno (Rev3)  # not connected
  Composant2 = Arduino Wireless SD Shield
  LED1 = LED - 5mm [color="Green (565nm)" package="5 mm [THT]"]
  LED2 = LED - 5mm [color="Red (633nm)" package="5 mm [THT]"]
  R1 = Resistor [tolerance=±5% resistance=220 package=THT]
  R2 = Resistor [tolerance=±5% resistance=220 package=THT]
  R3 = Photocell (LDR) [package=THT]
  R4 = Resistor [tolerance=±5% resistance=10k package=THT]

nets:
  N1: Composant2.A0, R3.pin_1, R4.Pin_0
  N2: Composant2.D9, R2.Pin_1
  N3: Composant2.D10, R1.Pin_1
  N4: Composant2.+5V, R4.Pin_1
  N5: Composant2.GND, LED1.cathode, LED2.cathode, R3.pin_0
  N6: LED1.anode, R1.Pin_0
  N7: LED2.anode, R2.Pin_0
