# Fritzing sketch circuit-alt (saved by Fritzing 0.9.1b)
breadboards: 1

parts:
  Composant1 = Arduino Yun
  U2 = 74HC595 [package="DIP16 [THT]"]
  R1 = Resistor [tolerance=±5% resistance=220 package=THT]
  R2 = Resistor [tolerance=±5% resistance=220 package=THT]
  R3 = Resistor [tolerance=±5% resistance=220 package=THT]
  R4 = Resistor [tolerance=±5% resistance=220 package=THT]
  R5 = Resistor [tolerance=±5% resistance=220 package=THT]
  R6 = Resistor [tolerance=±5% resistance=220 package=THT]
  R7 = Resistor [tolerance=±5% resistance=220 package=THT]
  R8 = Resistor [tolerance=±5% resistance=220 package=THT]
  LED1 = LED - 5mm [color="Yellow (595nm)" package="5 mm [THT]"]
  LED2 = LED - 5mm [color="Yellow (595nm)" package="5 mm [THT]"]
  LED3 = LED - 5mm [color="Yellow (595nm)" package="5 mm [THT]"]
  LED4 = LED - 5mm [color="Yellow (595nm)" package="5 mm [THT]"]
  LED5 = LED - 5mm [color="Yellow (595nm)" package="5 mm [THT]"]
  LED6 = LED - 5mm [color="Yellow (595nm)" package="5 mm [THT]"]
  LED7 = LED - 5mm [color="Green (565nm)" package="5 mm [THT]"]
  LED8 = LED - 5mm [color="Red (633nm)" package="5 mm [THT]"]
  Composant2 = Arduino Wireless SD Shield

nets:
  N1: Composant1.ICSP_SCK, Composant1.D13/SCK, Composant2.ARDUINO-RX(0)
  N2: Composant1.D10_PWM/SS, U2.SH_CP
  N3: Composant1.D5_PWM, Composant2.ARDUINO-TX(1)
  N4: Composant1.D6_PWM, U2.DS
  N5: Composant1.D7, U2.ST_CP
  5V: Composant1.5V, U2.MR, U2.VCC, Composant2.+5V
  GND: Composant1.GND, U2.GND, U2.OE, LED1.cathode, LED2.cathode, LED3.cathode, LED4.cathode, LED5.cathode, LED6.cathode, LED7.cathode, LED8.cathode, Composant2.GND
  N6: U2.Q1, R2.Pin_1
  N7: U2.Q2, R4.Pin_1
  N8: U2.Q3, R5.Pin_1
  N9: U2.Q4, R6.Pin_1
  N10: U2.Q5, R7.Pin_1
  N11: U2.Q6, R8.Pin_1
  N12: U2.Q7, R3.Pin_1
  N13: U2.Q0, R1.Pin_0
  N14: R1.Pin_1, LED7.anode
  N15: R2.Pin_0, LED8.anode
  N16: R3.Pin_0, LED6.anode
  N17: R4.Pin_0, LED1.anode
  N18: R5.Pin_0, LED2.anode
  N19: R6.Pin_0, LED3.anode
  N20: R7.Pin_0, LED4.anode
  N21: R8.Pin_0, LED5.anode
